# Fritzing sketch final (saved by Fritzing 0.9.3b)
breadboards: 1

parts:
  Raspberry_Pi_Zero2 = Raspberry Pi 3 [part_number=RPI-3-V1.2]
  J1 = Basic Force Sensing Resistor (FSR) [package=THT]
  R1 = Resistor [tolerance=±5% resistance=220 package=THT]
  J2 = Basic Servo
  J3 = Basic Servo
  U2 = 74HC595 [package="DIP16 [THT]"]  # not connected
  J4 = Basic Force Sensing Resistor (FSR) [package=THT]

nets:
  VCC: Raspberry_Pi_Zero2.3v3, J1.pin_0, J2.vcc, J3.vcc, J4.pin_0
  GND: Raspberry_Pi_Zero2.GND, R1.Pin_1, J2.gnd, J3.gnd
  N1: J1.pin_1, R1.Pin_0
